// Logisim project FlipFlops.circ as structural Verilog: 5 circuits, main circuit biestable
module biestable (
  input  in_1,
  input  in_2,
  output out_3
);

  wire and_1_out;

  and and_1 (and_1_out, in_2, out_3);
  or or_1 (out_3, in_1, and_1_out);
endmodule

module RS_Flip_Flop (
  input  in_1,
  input  in_2,
  output out_3,
  output out_4
);

  wire and_1_out, and_2_out, not_1_out, not_2_out;

  not not_1 (not_1_out, in_1);
  not not_2 (not_2_out, in_2);
  not not_3 (out_3, and_1_out);
  and and_1 (and_1_out, not_1_out, out_4);
  not not_4 (out_4, and_2_out);
  and and_2 (and_2_out, out_3, not_2_out);
endmodule

module D_Flip_Flop (
  input  in_1,
  output out_2,
  output out_3
);

  wire clock_1_out, not_1_out;

  Clock clock_1 (.out(clock_1_out));
  RS_Flip_Flop_Clk rs_flip_flop_clk_1 (
    .in_2(in_1), .in_3(clock_1_out), .in_4(not_1_out), .out_6(out_2), .out_7(out_3));  // open: in_1, in_5
  not not_1 (not_1_out, in_1);
endmodule

module RS_Flip_Flop_Clk (
  input  in_1,
  input  in_2,
  input  in_3,
  input  in_4,
  input  in_5,
  output out_6,
  output out_7
);

  wire and_1_out, and_2_out;

  and and_1 (and_1_out, in_4, in_3);
  and and_2 (and_2_out, in_3, in_2);
  nor nor_1 (out_6, in_1, and_1_out, out_7);
  nor nor_2 (out_7, out_6, and_2_out, in_5);
endmodule

module JK_Flip_Flop (
  input  in_1,
  input  in_2,
  input  in_3,
  input  in_4,
  output out_5,
  output out_6
);

  wire and_1_out, and_2_out, clock_1_out;

  Clock clock_1 (.out(clock_1_out));
  and and_1 (and_1_out, out_6, in_2);
  and and_2 (and_2_out, in_3, out_5);
  RS_Flip_Flop_Clk rs_flip_flop_clk_1 (
    .in_2(and_1_out), .in_3(clock_1_out), .in_4(and_2_out), .out_6(out_5), .out_7(out_6), .in_1(in_1),
    .in_5(in_4));
endmodule
