// Logisim project ejercicio3guia2.circ as structural Verilog: 9 circuits, main circuit Registro Simple
module Registro_Simple (
  input  in_1,
  input  in_2,
  input  in_3,
  input  in_4,
  input  in_5,
  input  in_6,
  output out_7,
  output out_8,
  output out_9,
  output out_10
);

  wire and_1_out, and_2_out, and_3_out, and_4_out, and_5_out, and_6_out, and_7_out, and_8_out;

  and and_1 (and_1_out, in_5, in_4);
  and and_2 (and_2_out, in_6, in_5);
  and and_3 (and_3_out, in_5, in_3);
  and and_4 (and_4_out, in_6, in_5);
  and and_5 (and_5_out, in_5, in_2);
  and and_6 (and_6_out, in_6, in_5);
  and and_7 (and_7_out, in_5, in_1);
  and and_8 (and_8_out, in_6, in_5);
  D_Flip_Flop d_ff_1 (.clk(and_2_out), .D(and_1_out), .Q(out_10));  // open: Qn, preset, en, reset
  D_Flip_Flop d_ff_2 (.clk(and_4_out), .D(and_3_out), .Q(out_9));  // open: Qn, preset, en, reset
  D_Flip_Flop d_ff_3 (.clk(and_6_out), .D(and_5_out), .Q(out_8));  // open: Qn, preset, en, reset
  D_Flip_Flop d_ff_4 (.clk(and_8_out), .D(and_7_out), .Q(out_7));  // open: Qn, preset, en, reset
endmodule

module ejercicio17 (
  input  in_1,
  input  in_2,
  input  in_3,
  input  in_4,
  input  in_5,
  input  in_6,
  input  in_7,
  output [3:0] out_8
);

  wire [3:0] registro_simple_1_out_7;
  wire [3:2] registro_simple_1_out_9;

  Registro_Simple registro_simple_1 (
    .in_1(in_1), .in_2(in_2), .in_3(in_3), .in_4(in_4), .in_5(in_5), .out_7(registro_simple_1_out_7[0]),
    .out_8(registro_simple_1_out_7[3]), .out_9(registro_simple_1_out_9[2]),
    .out_10(registro_simple_1_out_9[3]), .in_6(in_6));
  Multiplexer #(.width(4), .enable("false")) multiplexer_1 (
    .in0({registro_simple_1_out_9, registro_simple_1_out_7[3], registro_simple_1_out_7[0]}),
    .in1({{3{registro_simple_1_out_7[3]}}, registro_simple_1_out_7[0]}), .out(out_8), .sel(in_7));
endmodule

module ejercicio18 (
  input  [3:0] in_1,
  input  load,
  input  clk,
  input  read,
  output [3:0] out_5
);

  wire d_ff_1_q, not_1_out;
  wire [3:0] registro_simple_1_out_7;

  Registro_Simple registro_simple_1 (
    .in_1(in_1[0]), .in_2(in_1[1]), .in_3(in_1[2]), .in_4(in_1[3]), .in_5(load),
    .out_7(registro_simple_1_out_7[0]), .out_8(registro_simple_1_out_7[1]),
    .out_9(registro_simple_1_out_7[2]), .out_10(registro_simple_1_out_7[3]), .in_6(clk));
  D_Flip_Flop d_ff_1 (.clk(clk), .D(read), .Q(d_ff_1_q));  // open: Qn, preset, en, reset
  BitSelector #(.width(4), .group(4)) bitselector_1 (.in(registro_simple_1_out_7), .out(out_5), .sel(not_1_out));
  not not_1 (not_1_out, d_ff_1_q);
endmodule

module ejercicio19 (
  input  [3:0] in_1,
  input  clk,
  input  load,
  input  read,
  output [3:0] out_5
);

  wire [3:0] controlled_buffer_1_out, ejercicio18_1_out_5;

  assign controlled_buffer_1_out = load ? in_1 : 4'bz;  // Controlled_Buffer controlled_buffer_1
  assign out_5 = read ? ejercicio18_1_out_5 : 4'bz;  // Controlled_Buffer controlled_buffer_2
  ejercicio18 ejercicio18_1 (
    .in_1(controlled_buffer_1_out), .load(load), .clk(clk), .read(read), .out_5(ejercicio18_1_out_5));
endmodule

module ejercicio20 (
  input  [3:0] in_1,
  input  clk,
  input  Load,
  input  read,
  input  [3:0] in_5,
  input  [1:0] op,
  output [3:0] out_7
);

  wire [3:0] adder_1_out, multiplexer_1_out, registro_simple_1_out_7, registro_simple_2_out_7,
       subtractor_1_out;

  Registro_Simple registro_simple_1 (
    .in_1(in_1[0]), .in_2(in_1[1]), .in_3(in_1[2]), .in_4(in_1[3]), .in_5(Load),
    .out_7(registro_simple_1_out_7[0]), .out_8(registro_simple_1_out_7[1]),
    .out_9(registro_simple_1_out_7[2]), .out_10(registro_simple_1_out_7[3]), .in_6(clk));
  Registro_Simple registro_simple_2 (
    .in_1(in_5[0]), .in_2(in_5[1]), .in_3(in_5[2]), .in_4(in_5[3]), .in_5(Load),
    .out_7(registro_simple_2_out_7[0]), .out_8(registro_simple_2_out_7[1]),
    .out_9(registro_simple_2_out_7[2]), .out_10(registro_simple_2_out_7[3]), .in_6(clk));
  Adder #(.width(4)) adder_1 (
    .a(registro_simple_1_out_7), .b(registro_simple_2_out_7), .out(adder_1_out));  // open: cin, cout
  Subtractor #(.width(4)) subtractor_1 (
    .a(registro_simple_1_out_7), .b(registro_simple_2_out_7), .out(subtractor_1_out));  // open: bin, bout
  Multiplexer #(.select(2), .width(4), .enable("false")) multiplexer_1 (
    .in0(adder_1_out), .in1(subtractor_1_out), .out(multiplexer_1_out), .sel(op));  // open: in2, in3
  ejercicio18 ejercicio18_1 (.in_1(multiplexer_1_out), .load(Load), .clk(clk), .read(read), .out_5(out_7));
endmodule

module Lavarropas (
  input  Start
);

  wire cc_1_out_2;

  CC cc_1 (.out_2(cc_1_out_2));  // open: in_1
  // NOT_Gate not_1 has open pins: in=cc_1_out_2, out=open
  // AND_Gate and_1 is placed but not wired
endmodule

module Registro_Simple_6bits (
  input  in_1,
  input  in_2,
  input  in_3,
  input  in_4,
  input  in_5,
  input  in_6,
  input  in_7,
  input  in_8,
  output out_9,
  output out_10,
  output out_11,
  output out_12,
  output out_13,
  output out_14
);

  wire and_1_out, and_2_out, and_3_out, and_4_out, and_5_out, and_6_out, and_7_out, and_8_out, and_9_out,
       and_10_out, and_11_out, and_12_out;

  and and_1 (and_1_out, in_7, in_6);
  and and_2 (and_2_out, in_8, in_7);
  and and_3 (and_3_out, in_7, in_5);
  and and_4 (and_4_out, in_8, in_7);
  and and_5 (and_5_out, in_7, in_4);
  and and_6 (and_6_out, in_8, in_7);
  and and_7 (and_7_out, in_7, in_3);
  and and_8 (and_8_out, in_8, in_7);
  and and_9 (and_9_out, in_7, in_2);
  and and_10 (and_10_out, in_8, in_7);
  and and_11 (and_11_out, in_1, in_7);
  and and_12 (and_12_out, in_7, in_8);
  D_Flip_Flop d_ff_1 (.clk(and_2_out), .D(and_1_out), .Q(out_14));  // open: Qn, preset, en, reset
  D_Flip_Flop d_ff_2 (.clk(and_4_out), .D(and_3_out), .Q(out_13));  // open: Qn, preset, en, reset
  D_Flip_Flop d_ff_3 (.clk(and_6_out), .D(and_5_out), .Q(out_12));  // open: Qn, preset, en, reset
  D_Flip_Flop d_ff_4 (.clk(and_8_out), .D(and_7_out), .Q(out_11));  // open: Qn, preset, en, reset
  D_Flip_Flop d_ff_5 (.clk(and_10_out), .D(and_9_out), .Q(out_10));  // open: Qn, preset, en, reset
  D_Flip_Flop d_ff_6 (.clk(and_12_out), .D(and_11_out), .Q(out_9));  // open: Qn, preset, en, reset
endmodule

module Registro_Restador (
  input  Reset,
  input  Clk,
  output [5:0] out_3
);

  wire comparator_1_lt, or_1_out;
  wire [5:0] multiplexer_1_out, multiplexer_2_out, subtractor_1_out;

  Subtractor #(.width(6)) subtractor_1 (.a(out_3), .b(6'b000001), .out(subtractor_1_out));  // open: bin, bout
  Multiplexer #(.width(6), .enable("false")) multiplexer_1 (
    .in0(multiplexer_2_out), .in1(6'b011110), .out(multiplexer_1_out), .sel(Reset));
  Multiplexer #(.width(6), .enable("false")) multiplexer_2 (
    .in0({6{1'b0}}), .in1(subtractor_1_out), .out(multiplexer_2_out), .sel(comparator_1_lt));
  Registro_Simple_6bits registro_simple_6bits_1 (
    .in_1(multiplexer_1_out[5]), .in_2(multiplexer_1_out[4]), .in_3(multiplexer_1_out[3]),
    .in_4(multiplexer_1_out[2]), .in_5(multiplexer_1_out[1]), .in_6(multiplexer_1_out[0]), .in_7(Clk),
    .in_8(or_1_out), .out_11(out_3[3]), .out_12(out_3[2]), .out_13(out_3[1]), .out_14(out_3[0]),
    .out_10(out_3[4]), .out_9(out_3[5]));
  or or_1 (or_1_out, Reset, Clk);
  Comparator #(.width(6), .mode("unsigned")) comparator_1 (
    .a({6{1'b0}}), .b(subtractor_1_out), .lt(comparator_1_lt));  // open: gt, eq
endmodule

module CC (
  input  [15:0] in_1,
  output out_2
);

  Comparator #(.width(16), .mode("unsigned")) comparator_1 (.a(16'h1770), .b(in_1), .eq(out_2));  // open: gt, lt
endmodule
