// Logisim project ejercicio4y5.circ as structural Verilog: 2 circuits, main circuit main
module main (
  input  in_1,
  input  in_2,
  input  in_3,
  output out_4,
  output out_5
);

  wire nand_2_out;

  nand nand_1 (out_5, in_3, in_3);
  nand nand_2 (nand_2_out, in_1, in_2);
  nand nand_3 (out_4, nand_2_out, nand_2_out);
endmodule

module ejercicio5 (
  input  in_1,
  input  in_2,
  input  in_3,
  output out_4
);

  wire nor_1_out, not_1_out, not_2_out, not_3_out, not_4_out;

  not not_1 (not_1_out, in_1);
  not not_2 (not_2_out, in_2);
  not not_3 (not_3_out, in_3);
  nor nor_1 (nor_1_out, not_1_out, not_2_out);
  not not_4 (not_4_out, nor_1_out);
  nor nor_2 (out_4, not_4_out, not_3_out);
endmodule
