// Logisim project ejercicio9al12(creoqueviejo).circ as structural Verilog: 6 circuits, main circuit ejercicio9
module ejercicio9 (
  input  in_1,
  input  in_2,
  output out_3,
  output out_4,
  output out_5,
  output out_6
);

  wire not_1_out, not_2_out;

  not not_1 (not_1_out, in_1);
  not not_2 (not_2_out, in_2);
  nor nor_1 (out_3, in_1, in_2);
  nor nor_2 (out_4, not_1_out, in_2);
  nor nor_3 (out_5, not_2_out, in_1);
  and and_1 (out_6, in_2, in_1);
endmodule

module ejercicio9bis (
  input  in_1,
  input  in_2,
  input  in_3,
  output out_4,
  output out_5,
  output out_6,
  output out_7
);

  wire ejercicio9_1_out_3, ejercicio9_1_out_4, ejercicio9_1_out_5, ejercicio9_1_out_6;

  ejercicio9 ejercicio9_1 (
    .in_1(in_1), .in_2(in_2), .out_3(ejercicio9_1_out_3), .out_4(ejercicio9_1_out_4),
    .out_5(ejercicio9_1_out_5), .out_6(ejercicio9_1_out_6));
  and and_1 (out_4, in_3, ejercicio9_1_out_3);
  and and_2 (out_5, in_3, ejercicio9_1_out_4);
  and and_3 (out_6, in_3, ejercicio9_1_out_5);
  and and_4 (out_7, ejercicio9_1_out_6, in_3);
endmodule

module ejercicio10 (
  input  in_1,
  input  in_2,
  input  in_3,
  input  in_4,
  output out_5,
  output out_6,
  output out_7,
  output out_8
);

  wire and_2_out, and_3_out, and_4_out, and_5_out, not_1_out, not_2_out, not_3_out;

  not not_1 (not_1_out, in_1);
  not not_2 (not_2_out, in_1);
  not not_3 (not_3_out, in_1);
  and and_1 (out_5, not_1_out, in_2);
  and and_2 (and_2_out, in_1, in_2);
  and and_3 (and_3_out, not_2_out, in_3);
  and and_4 (and_4_out, in_1, in_3);
  and and_5 (and_5_out, not_3_out, in_4);
  and and_6 (out_8, in_4, in_1);
  or or_1 (out_6, and_2_out, and_3_out);
  or or_2 (out_7, and_4_out, and_5_out);
endmodule

module ejercicio11 (
  input  in_1,
  input  in_2,
  input  in_3,
  output out_4,
  output out_5
);

  wire and_1_out, and_2_out, and_3_out, and_4_out, not_1_out, or_1_out, xnor_1_out, xor_1_out;

  or or_1 (or_1_out, in_3, in_2);
  and and_1 (and_1_out, in_3, in_2);
  and and_2 (and_2_out, or_1_out, in_1);
  xnor xnor_1 (xnor_1_out, in_3, in_2);
  and and_3 (and_3_out, xnor_1_out, in_1);
  not not_1 (not_1_out, in_1);
  xor xor_1 (xor_1_out, in_3, in_2);
  or or_2 (out_4, and_1_out, and_2_out);
  or or_3 (out_5, and_3_out, and_4_out);
  and and_4 (and_4_out, not_1_out, xor_1_out);
endmodule

module ejercicio12 (
  input  in_1,
  input  in_2,
  input  in_3,
  input  in_4,
  input  in_5,
  input  in_6,
  input  in_7,
  input  in_8,
  input  in_9,
  output out_10,
  output out_11,
  output out_12,
  output out_13,
  output out_14
);

  wire ejercicio11_1_out_4, ejercicio11_2_out_4, ejercicio11_3_out_4;

  ejercicio11 ejercicio11_1 (.in_1(in_6), .in_2(in_2), .in_3(in_1), .out_4(ejercicio11_1_out_4), .out_5(out_10));
  ejercicio11 ejercicio11_2 (
    .in_1(in_7), .in_2(in_3), .in_3(ejercicio11_1_out_4), .out_4(ejercicio11_2_out_4), .out_5(out_11));
  ejercicio11 ejercicio11_3 (
    .in_1(in_8), .in_2(in_4), .in_3(ejercicio11_2_out_4), .out_4(ejercicio11_3_out_4), .out_5(out_12));
  ejercicio11 ejercicio11_4 (.in_1(in_9), .in_2(in_5), .in_3(ejercicio11_3_out_4), .out_4(out_14), .out_5(out_13));
endmodule

module ejercicio12b (
  input  in_1,
  input  in_2,
  input  in_3,
  input  in_4,
  input  in_5,
  input  in_6,
  input  in_7,
  input  in_8,
  input  in_9,
  output out_10,
  output out_11,
  output out_12,
  output out_13,
  output out_14,
  output out_15,
  output out_16,
  output out_17
);

  wire and_1_out;

  and and_1 (and_1_out, in_9, in_2);
  xor xor_1 (out_15, out_13, and_1_out);
  ejercicio12 ejercicio12_1 (
    .in_1(in_1), .in_2(in_5), .in_3(in_4), .in_4(in_3), .in_5(in_2), .in_6(in_9), .in_7(in_8), .in_8(in_7),
    .in_9(in_6), .out_10(out_10), .out_11(out_11), .out_12(out_12), .out_13(out_13), .out_14(out_16));
  nor nor_1 (out_17, out_13, out_12, out_11, out_10);

  assign out_14 = out_13;
endmodule
