// Logisim project ejercicios678.circ as structural Verilog: 4 circuits, main circuit ejercicio7
module ejercicio7 (
  input  in_1,
  input  in_2,
  input  in_3,
  output out_4,
  output out_5,
  output out_6,
  output out_7
);

  wire and_1_out, and_2_out, and_3_out, nor_1_out, not_1_out, not_2_out;

  // NAND_Gate nand_1 is placed but not wired
  nor nor_1 (nor_1_out, in_1, in_2);
  not not_1 (not_1_out, in_1);
  and and_1 (and_1_out, not_1_out, in_2);
  not not_2 (not_2_out, in_2);
  and and_2 (and_2_out, not_2_out, in_1);
  and and_3 (and_3_out, in_1, in_2);
  and and_4 (out_4, nor_1_out, in_3);
  and and_5 (out_5, and_1_out, in_3);
  and and_6 (out_6, and_2_out, in_3);
  and and_7 (out_7, and_3_out, in_3);
endmodule

module Ejercicio6 (
  input  in_1,
  input  in_2,
  input  in_3,
  output out_4
);

  wire and_1_out, not_1_out;

  not not_1 (not_1_out, in_1);
  and and_1 (and_1_out, not_1_out, in_2, in_3);
  or or_1 (out_4, in_1, and_1_out);
endmodule

module ejercicio8 (
  input  in_1,
  input  in_2,
  input  in_3,
  input  in_4,
  output out_5,
  output out_6,
  output out_7
);

  wire not_1_out, xor_1_out, xor_2_out;

  not not_1 (not_1_out, in_1);
  xor xor_1 (xor_1_out, not_1_out, in_2);
  xor xor_2 (xor_2_out, not_1_out, in_3);
  or or_1 (out_6, xor_2_out, in_4);
  or or_2 (out_7, xor_1_out, in_4);
  ejercicio8bis ejercicio8bis_1 (.in_1(in_1), .in_2(in_2), .in_3(in_4), .in_4(in_3), .out_5(out_5));
endmodule

module ejercicio8bis (
  input  in_1,
  input  in_2,
  input  in_3,
  input  in_4,
  output out_5
);

  wire and_1_out, and_2_out, and_3_out, or_1_out, or_2_out;

  and and_1 (and_1_out, in_1, or_1_out);
  or or_1 (or_1_out, in_2, in_3, in_4);
  and and_2 (and_2_out, in_2, in_4);
  or or_2 (or_2_out, in_2, in_4);
  and and_3 (and_3_out, or_2_out, in_3);
  or or_3 (out_5, and_1_out, and_2_out, and_3_out);
endmodule
