// Logisim project TallerLogica-AndyFelder.circ as structural Verilog: 17 circuits, main circuit verificador
module sumador_simple (
  input  a,
  input  b,
  output S,
  output Cout
);

  xor xor_1 (S, a, b);
  and and_1 (Cout, a, b);
endmodule

module sumador_completo (
  input  Cin,
  input  A,
  input  B,
  output S,
  output Cout
);

  wire sumador_simple_1_cout, sumador_simple_1_s, sumador_simple_2_cout;

  sumador_simple sumador_simple_1 (.a(A), .b(B), .S(sumador_simple_1_s), .Cout(sumador_simple_1_cout));
  sumador_simple sumador_simple_2 (.a(Cin), .b(sumador_simple_1_s), .S(S), .Cout(sumador_simple_2_cout));
  or or_1 (Cout, sumador_simple_2_cout, sumador_simple_1_cout);
endmodule

module sumador_4 (
  input  [3:0] A,
  input  [3:0] B,
  output [3:0] S,
  output Cout
);

  wire sumador_completo_1_cout, sumador_completo_2_cout, sumador_completo_3_cout;

  sumador_completo sumador_completo_1 (.A(A[0]), .B(B[0]), .Cin(1'b0), .S(S[0]), .Cout(sumador_completo_1_cout));
  sumador_completo sumador_completo_2 (
    .A(A[1]), .B(B[1]), .Cin(sumador_completo_1_cout), .S(S[1]), .Cout(sumador_completo_2_cout));
  sumador_completo sumador_completo_3 (
    .A(A[2]), .B(B[2]), .Cin(sumador_completo_2_cout), .S(S[2]), .Cout(sumador_completo_3_cout));
  sumador_completo sumador_completo_4 (.A(A[3]), .B(B[3]), .Cin(sumador_completo_3_cout), .S(S[3]), .Cout(Cout));
  Hex_Digit_Display hex_digit_display_1 (.value(S));  // open: dp
endmodule

module comparador_cero (
  input  [3:0] A,
  output Z
);

  wire and_1_out, and_2_out, not_1_out, not_2_out, not_3_out, not_4_out;

  not not_1 (not_1_out, A[0]);
  not not_2 (not_2_out, A[1]);
  not not_3 (not_3_out, A[2]);
  and and_1 (and_1_out, not_1_out, not_2_out);
  not not_4 (not_4_out, A[3]);
  and and_2 (and_2_out, not_3_out, not_4_out);
  and and_3 (Z, and_1_out, and_2_out);
endmodule

module sumador_flags (
  input  Cin,
  input  [3:0] A,
  input  [3:0] B,
  output [3:0] S,
  output N,
  output Z,
  output V,
  output C
);

  wire and_1_out, and_2_out, not_1_out, not_2_out, not_3_out, sumador_completo_1_cout,
       sumador_completo_2_cout, sumador_completo_3_cout;

  not not_1 (not_1_out, N);
  not not_2 (not_2_out, A[3]);
  not not_3 (not_3_out, B[3]);
  sumador_completo sumador_completo_1 (.A(A[0]), .B(B[0]), .Cin(Cin), .S(S[0]), .Cout(sumador_completo_1_cout));
  sumador_completo sumador_completo_2 (
    .A(A[1]), .B(B[1]), .Cin(sumador_completo_1_cout), .S(S[1]), .Cout(sumador_completo_2_cout));
  and and_1 (and_1_out, not_1_out, A[3], B[3]);
  and and_2 (and_2_out, N, not_2_out, not_3_out);
  sumador_completo sumador_completo_3 (
    .A(A[2]), .B(B[2]), .Cin(sumador_completo_2_cout), .S(S[2]), .Cout(sumador_completo_3_cout));
  sumador_completo sumador_completo_4 (.A(A[3]), .B(B[3]), .Cin(sumador_completo_3_cout), .S(N), .Cout(C));
  or or_1 (V, and_1_out, and_2_out);
  Hex_Digit_Display hex_digit_display_1 (.value({N, S[2:0]}));  // open: dp
  comparador_cero comparador_cero_1 (.A({N, S[2:0]}), .Z(Z));

  assign S[3] = N;
endmodule

module incrementador_4 (
  input  Cin,
  input  [3:0] A,
  output [3:0] S,
  output Cout
);

  sumador_4 sumador_4_1 (.A(4'b0001), .S(S), .B(A), .Cout(Cout));
  Hex_Digit_Display hex_digit_display_1 (.value(S));  // open: dp
endmodule

module inversor_4 (
  input  [3:0] A,
  input  INV,
  output [3:0] S
);

  wire [3:0] calculoinverso_1_out_2;

  calculoInverso calculoinverso_1 (.in_1(A), .out_2(calculoinverso_1_out_2));  // open: out_3
  Multiplexer #(.width(4)) multiplexer_1 (.in0(A), .in1(calculoinverso_1_out_2), .out(S), .sel(INV));  // open: en
  Hex_Digit_Display hex_digit_display_1 (.value(S));  // open: dp
endmodule

module ALU_mal (
  input  [3:0] A,
  input  [3:0] B,
  input  [1:0] OP,
  output N,
  output Z,
  output V,
  output C,
  output [3:0] S
);

  wire andbitabit_1_n, andbitabit_1_z, orbitabit_1_n, orbitabit_1_z, resta_4_1_co, resta_4_1_n, resta_4_1_v,
       resta_4_1_z, sumador_flags_1_c, sumador_flags_1_n, sumador_flags_1_v, sumador_flags_1_z;
  wire [3:0] andbitabit_1_s, orbitabit_1_s, resta_4_1_out_3, sumador_flags_1_s;

  sumador_flags sumador_flags_1 (
    .A(A), .B(B), .Cin(1'b0), .S(sumador_flags_1_s), .N(sumador_flags_1_n), .Z(sumador_flags_1_z),
    .V(sumador_flags_1_v), .C(sumador_flags_1_c));
  resta_4 resta_4_1 (
    .a(A), .b(B), .out_3(resta_4_1_out_3), .N(resta_4_1_n), .z(resta_4_1_z), .V(resta_4_1_v),
    .co(resta_4_1_co));
  andBitABit andbitabit_1 (.A(A), .b(B), .s(andbitabit_1_s), .N(andbitabit_1_n), .Z(andbitabit_1_z));
  OrBitABit orbitabit_1 (.A(A), .b(B), .s(orbitabit_1_s), .N(orbitabit_1_n), .Z(orbitabit_1_z));
  Multiplexer #(.select(2)) multiplexer_1 (
    .in0(sumador_flags_1_c), .in1(resta_4_1_co), .in2(1'b0), .in3(1'b0), .out(C), .sel(OP));  // open: en
  Multiplexer #(.select(2), .width(4)) multiplexer_2 (
    .in0(sumador_flags_1_s), .in1(resta_4_1_out_3), .in2(andbitabit_1_s), .in3(orbitabit_1_s), .out(S),
    .sel(OP));  // open: en
  Multiplexer #(.select(2)) multiplexer_3 (
    .in0(sumador_flags_1_z), .in1(resta_4_1_z), .in2(andbitabit_1_n), .in3(orbitabit_1_n), .out(Z), .sel(OP));  // open: en
  Multiplexer #(.select(2)) multiplexer_4 (
    .in0(sumador_flags_1_v), .in1(resta_4_1_v), .in2(1'b0), .in3(1'b0), .out(V), .sel(OP));  // open: en
  Multiplexer #(.select(2)) multiplexer_5 (
    .in0(sumador_flags_1_n), .in1(resta_4_1_n), .in2(andbitabit_1_z), .in3(orbitabit_1_z), .out(N), .sel(OP));  // open: en
  Hex_Digit_Display hex_digit_display_1 (.value(S));  // open: dp
endmodule

module verificador (
  output [3:0] a,
  output [3:0] b,
  output [1:0] Op,
  output N,
  output Z,
  output V,
  output C,
  output [3:0] Res,
  output halt
);

  wire clock_1_out;

  Clock clock_1 (.out(clock_1_out));
  Counter #(.width(10), .max('h3ff)) counter_1 (
    .Q({Op, b, a}), .carry(halt), .clk(clock_1_out));  // open: load, D, count, clr
  ALU_mal alu_mal_1 (.A(a), .B(b), .OP(Op), .N(N), .Z(Z), .V(V), .C(C), .S(Res));
endmodule

module calculoInverso (
  input  [3:0] in_1,
  output [3:0] out_2,
  output out_3
);

  wire [3:0] calculoopuesto_1_s0;

  calculoOpuesto calculoopuesto_1 (
    .e0(in_1[0]), .e1(in_1[1]), .e2(in_1[2]), .e3(in_1[3]), .s0(calculoopuesto_1_s0[0]),
    .s1(calculoopuesto_1_s0[1]), .s2(calculoopuesto_1_s0[2]), .s3(calculoopuesto_1_s0[3]));
  incrementador_4 incrementador_4_1 (.A(calculoopuesto_1_s0), .Cin(1'b0), .S(out_2), .Cout(out_3));
endmodule

module calculoOpuesto (
  input  e0,
  input  e1,
  input  e2,
  input  e3,
  output s0,
  output s1,
  output s2,
  output s3
);

  not not_1 (s0, e0);
  not not_2 (s1, e1);
  not not_3 (s2, e2);
  not not_4 (s3, e3);
endmodule

// Z
module resta_4 (
  input  [3:0] a,
  input  [3:0] b,
  output [3:0] out_3,
  output N,
  output z,
  output V,
  output co
);

  wire comparador_cero_1_z, not_1_out, sumador_flags_1_c;
  wire [3:0] inversor_4_1_s;

  inversor_4 inversor_4_1 (.A(b), .INV(1'b1), .S(inversor_4_1_s));
  sumador_flags sumador_flags_1 (
    .A(a), .B(inversor_4_1_s), .Cin(1'b0), .S(out_3), .N(N), .Z(z), .V(V), .C(sumador_flags_1_c));
  comparador_cero comparador_cero_1 (.A(b), .Z(comparador_cero_1_z));
  not not_1 (not_1_out, sumador_flags_1_c);
  xor xor_1 (co, not_1_out, comparador_cero_1_z);
endmodule

module resta_simple (
  input  bi,
  input  a,
  input  b,
  output s,
  output bo
);

  wire and_1_out, and_2_out, not_1_out, not_2_out, xor_1_out;

  xor xor_1 (xor_1_out, a, b);
  not not_1 (not_1_out, a);
  and and_1 (and_1_out, not_1_out, b);
  not not_2 (not_2_out, xor_1_out);
  and and_2 (and_2_out, bi, not_2_out);
  xor xor_2 (s, xor_1_out, bi);
  or or_1 (bo, and_2_out, and_1_out);
endmodule

module andBitABit (
  input  [3:0] A,
  input  [3:0] b,
  output [3:0] s,
  output N,
  output Z
);

  and and_1 (s[2], A[2], b[2]);
  and and_2 (N, A[3], b[3]);
  and and_3 (s[0], A[0], b[0]);
  and and_4 (s[1], A[1], b[1]);
  comparador_cero comparador_cero_1 (.A({N, s[2:0]}), .Z(Z));

  assign s[3] = N;
endmodule

module OrBitABit (
  input  [3:0] A,
  input  [3:0] b,
  output [3:0] s,
  output N,
  output Z
);

  or or_1 (s[2], A[2], b[2]);
  or or_2 (N, A[3], b[3]);
  or or_3 (s[0], A[0], b[0]);
  or or_4 (s[1], A[1], b[1]);
  comparador_cero comparador_cero_1 (.A({N, s[2:0]}), .Z(Z));

  assign s[3] = N;
endmodule

module ALU_prueba (
  input  [3:0] A,
  input  [3:0] B,
  input  [1:0] OP,
  output N,
  output Z,
  output V,
  output C,
  output [3:0] S
);

  wire resta_4_1_co, resta_4_1_n, resta_4_1_v, resta_4_1_z, sumador_flags_1_c, sumador_flags_1_n,
       sumador_flags_1_v, sumador_flags_1_z;
  wire [3:0] andbitabit_1_s, orbitabit_1_s, resta_4_1_out_3, sumador_flags_1_s;

  sumador_flags sumador_flags_1 (
    .A(A), .B(B), .Cin(1'b0), .S(sumador_flags_1_s), .N(sumador_flags_1_n), .Z(sumador_flags_1_z),
    .V(sumador_flags_1_v), .C(sumador_flags_1_c));
  resta_4 resta_4_1 (
    .a(A), .b(B), .out_3(resta_4_1_out_3), .N(resta_4_1_n), .z(resta_4_1_z), .V(resta_4_1_v),
    .co(resta_4_1_co));
  andBitABit andbitabit_1 (.A(A), .b(B), .s(andbitabit_1_s));  // open: N, Z
  OrBitABit orbitabit_1 (.A(A), .b(B), .s(orbitabit_1_s));  // open: N, Z
  Multiplexer #(.select(2)) multiplexer_1 (
    .in0(sumador_flags_1_c), .in1(resta_4_1_co), .in2(1'b0), .in3(1'b0), .out(C), .sel(OP));  // open: en
  Multiplexer #(.select(2), .width(4)) multiplexer_2 (
    .in0(sumador_flags_1_s), .in1(resta_4_1_out_3), .in2(andbitabit_1_s), .in3(orbitabit_1_s), .out(S),
    .sel(OP));  // open: en
  Multiplexer #(.select(2)) multiplexer_3 (
    .in0(sumador_flags_1_z), .in1(resta_4_1_z), .in2(1'b0), .in3(1'b0), .out(Z), .sel(OP));  // open: en
  Multiplexer #(.select(2)) multiplexer_4 (
    .in0(sumador_flags_1_v), .in1(resta_4_1_v), .in2(1'b0), .in3(1'b0), .out(V), .sel(OP));  // open: en
  Multiplexer #(.select(2)) multiplexer_5 (
    .in0(sumador_flags_1_n), .in1(resta_4_1_n), .in2(1'b0), .in3(1'b0), .out(N), .sel(OP));  // open: en
  Hex_Digit_Display hex_digit_display_1 (.value(S));  // open: dp
endmodule

module ALU (
  input  [3:0] A,
  input  [3:0] B,
  input  [1:0] OP,
  output N,
  output Z,
  output V,
  output C,
  output [3:0] S
);

  wire andbitabit_1_z, orbitabit_1_n, orbitabit_1_z, resta_4_1_co, resta_4_1_n, resta_4_1_v,
       sumador_flags_1_c, sumador_flags_1_n, sumador_flags_1_v;
  wire [3:0] andbitabit_1_s, orbitabit_1_s, resta_4_1_out_3, sumador_flags_1_s;

  sumador_flags sumador_flags_1 (
    .A(A), .B(B), .Cin(1'b0), .S(sumador_flags_1_s), .N(sumador_flags_1_n), .V(sumador_flags_1_v),
    .C(sumador_flags_1_c));  // open: Z
  resta_4 resta_4_1 (
    .a(A), .b(B), .out_3(resta_4_1_out_3), .N(resta_4_1_n), .V(resta_4_1_v), .co(resta_4_1_co));  // open: z
  andBitABit andbitabit_1 (.A(A), .b(B), .s(andbitabit_1_s), .Z(andbitabit_1_z));  // open: N
  OrBitABit orbitabit_1 (.A(A), .b(B), .s(orbitabit_1_s), .N(orbitabit_1_n), .Z(orbitabit_1_z));
  Multiplexer #(.select(2)) multiplexer_1 (
    .in0(sumador_flags_1_c), .in1(resta_4_1_co), .in2(1'b0), .in3(1'b0), .out(C), .sel(OP));  // open: en
  Multiplexer #(.select(2), .width(4)) multiplexer_2 (
    .in0(sumador_flags_1_s), .in1(resta_4_1_out_3), .in2(andbitabit_1_s), .in3(orbitabit_1_s), .out(S),
    .sel(OP));  // open: en
  Multiplexer #(.select(2)) multiplexer_3 (
    .in0(sumador_flags_1_v), .in1(resta_4_1_v), .in2(1'b0), .in3(1'b0), .out(V), .sel(OP));  // open: en
  Multiplexer #(.select(2)) multiplexer_4 (
    .in0(sumador_flags_1_n), .in1(resta_4_1_n), .in2(andbitabit_1_z), .in3(orbitabit_1_z), .out(N), .sel(OP));  // open: en
  comparador_cero comparador_cero_1 (.A(S), .Z(Z));
  Hex_Digit_Display hex_digit_display_1 (.value(S));  // open: dp
endmodule
