// Logisim project TallerLogica-Combinatorios.circ as structural Verilog: 15 circuits, main circuit verificador
module sumador_simple (
  input  a,
  input  b,
  output S,
  output Cout
);

  xor xor_1 (S, a, b);
  and and_1 (Cout, a, b);
endmodule

module sumador_completo (
  input  Cin,
  input  A,
  input  B,
  output S,
  output Cout
);

  wire sumador_simple_1_cout, sumador_simple_2_cout, sumador_simple_2_s;

  sumador_simple sumador_simple_1 (.a(Cin), .b(sumador_simple_2_s), .S(S), .Cout(sumador_simple_1_cout));
  sumador_simple sumador_simple_2 (.a(A), .b(B), .S(sumador_simple_2_s), .Cout(sumador_simple_2_cout));
  or or_1 (Cout, sumador_simple_1_cout, sumador_simple_2_cout);
endmodule

module sumador_4 (
  input  Cin,
  input  [3:0] A,
  input  [3:0] B,
  output [3:0] S,
  output Cout
);

  wire sumador_completo_1_cout, sumador_completo_2_cout, sumador_completo_3_cout;

  sumador_completo sumador_completo_1 (.A(A[0]), .B(B[0]), .Cin(Cin), .S(S[0]), .Cout(sumador_completo_1_cout));
  sumador_completo sumador_completo_2 (
    .A(A[1]), .B(B[1]), .Cin(sumador_completo_1_cout), .S(S[1]), .Cout(sumador_completo_2_cout));
  sumador_completo sumador_completo_3 (
    .A(A[2]), .B(B[2]), .Cin(sumador_completo_2_cout), .S(S[2]), .Cout(sumador_completo_3_cout));
  sumador_completo sumador_completo_4 (.A(A[3]), .B(B[3]), .Cin(sumador_completo_3_cout), .S(S[3]), .Cout(Cout));
  Hex_Digit_Display hex_digit_display_1 (.value(S));  // open: dp
endmodule

module comparador_cero (
  input  [3:0] A,
  output Z
);

  wire and_1_out, and_2_out, not_1_out, not_2_out, not_3_out, not_4_out;

  not not_1 (not_1_out, A[0]);
  not not_2 (not_2_out, A[1]);
  not not_3 (not_3_out, A[2]);
  not not_4 (not_4_out, A[3]);
  and and_1 (and_1_out, not_1_out, not_2_out);
  and and_2 (and_2_out, not_3_out, not_4_out);
  and and_3 (Z, and_1_out, and_2_out);
endmodule

module sumador_flags (
  input  Cin,
  input  [3:0] A,
  input  [3:0] B,
  output [3:0] S,
  output N,
  output Z,
  output V,
  output C
);

  wire and_1_out, and_2_out, not_1_out, not_2_out, not_3_out, or_1_out, or_2_out;

  sumador_4 sumador_4_1 (.Cin(Cin), .A(A), .S({N, S[2:0]}), .B(B), .Cout(C));
  and and_1 (and_1_out, A[3], B[3]);
  not not_1 (not_1_out, and_1_out);
  not not_2 (not_2_out, or_1_out);
  or or_1 (or_1_out, B[3], A[3]);
  not not_3 (not_3_out, or_2_out);
  or or_2 (or_2_out, N, not_1_out);
  and and_2 (and_2_out, N, not_2_out);
  Hex_Digit_Display hex_digit_display_1 (.value({N, S[2:0]}));  // open: dp
  comparador_cero comparador_cero_1 (.A({N, S[2:0]}), .Z(Z));
  or or_3 (V, not_3_out, and_2_out);

  assign S[3] = N;
endmodule

module incrementador_4 (
  input  [3:0] A,
  output [3:0] S
);

  sumador_4 sumador_4_1 (.Cin(1'b0), .A(A), .S(S), .B(4'b0001));  // open: Cout
  Hex_Digit_Display hex_digit_display_1 (.value(S));  // open: dp
endmodule

module inversor_4 (
  input  [3:0] A,
  input  INV,
  output [3:0] S
);

  wire [3:0] xor_1_out;

  xor xor_1 (xor_1_out[0], A[0], INV);
  xor xor_2 (xor_1_out[1], A[1], INV);
  xor xor_3 (xor_1_out[2], A[2], INV);
  xor xor_4 (xor_1_out[3], A[3], INV);
  sumador_4 sumador_4_1 (.Cin(1'b0), .A(xor_1_out), .S(S), .B({3'b000, INV}));  // open: Cout
  Hex_Digit_Display hex_digit_display_1 (.value(S));  // open: dp
endmodule

module ALU (
  input  [3:0] A,
  input  [3:0] B,
  input  [1:0] OP,
  output N,
  output Z,
  output V,
  output C,
  output [3:0] S
);

  wire decoder_1_out_2, decoder_1_out_3, decoder_1_out_4, decoder_1_out_5;
  wire [1:0] andbitabit_1_zero, orbitabit_1_out_3;
  wire [3:0] and4entradas_1_out_3, and4entradas_2_out_3, and4entradas_3_out_3, and4entradas_4_out_3,
       and4entradas_5_out_3, and4entradas_6_out_3, and4entradas_7_out_3, and4entradas_8_out_3,
       andbitabit_1_out_5, orbitabit_1_out_5, restador_flags_1_n, restador_flags_1_s, sumador_flags_1_n,
       sumador_flags_1_s;

  decoder decoder_1 (
    .OP(OP), .out_2(decoder_1_out_2), .out_3(decoder_1_out_3), .out_4(decoder_1_out_4),
    .out_5(decoder_1_out_5));
  and4entradas and4entradas_1 (.A(A), .in_2(decoder_1_out_2), .out_3(and4entradas_1_out_3));
  and4entradas and4entradas_2 (.A(B), .in_2(decoder_1_out_2), .out_3(and4entradas_2_out_3));
  and4entradas and4entradas_3 (.A(A), .in_2(decoder_1_out_3), .out_3(and4entradas_3_out_3));
  and4entradas and4entradas_4 (.A(B), .in_2(decoder_1_out_3), .out_3(and4entradas_4_out_3));
  and4entradas and4entradas_5 (.A(A), .in_2(decoder_1_out_4), .out_3(and4entradas_5_out_3));
  and4entradas and4entradas_6 (.A(B), .in_2(decoder_1_out_4), .out_3(and4entradas_6_out_3));
  orbitabit orbitabit_1 (
    .in_1(and4entradas_7_out_3), .in_2(and4entradas_8_out_3), .out_5(orbitabit_1_out_5),
    .out_3(orbitabit_1_out_3[0]), .out_4(orbitabit_1_out_3[1]));
  and4entradas and4entradas_7 (.A(A), .in_2(decoder_1_out_5), .out_3(and4entradas_7_out_3));
  and4entradas and4entradas_8 (.A(B), .in_2(decoder_1_out_5), .out_3(and4entradas_8_out_3));
  sumador_flags sumador_flags_1 (
    .A(and4entradas_1_out_3), .B(and4entradas_2_out_3), .Cin(1'b0), .S(sumador_flags_1_s),
    .N(sumador_flags_1_n[0]), .Z(sumador_flags_1_n[1]), .V(sumador_flags_1_n[2]), .C(sumador_flags_1_n[3]));
  restador_flags restador_flags_1 (
    .A(and4entradas_3_out_3), .B(and4entradas_4_out_3), .Cin(1'b0), .S(restador_flags_1_s),
    .N(restador_flags_1_n[0]), .Z(restador_flags_1_n[1]), .V(restador_flags_1_n[2]), .C(restador_flags_1_n[3]));
  andbitabit andbitabit_1 (
    .in_1(and4entradas_5_out_3), .in_2(and4entradas_6_out_3), .out_5(andbitabit_1_out_5),
    .Zero(andbitabit_1_zero[0]), .Z(andbitabit_1_zero[1]));
  Multiplexer #(.select(2), .width(4), .enable("false")) multiplexer_1 (
    .in0(sumador_flags_1_n), .in1(restador_flags_1_n), .in2({2'b00, andbitabit_1_zero}),
    .in3({2'b00, orbitabit_1_out_3}), .out({C, V, Z, N}), .sel(OP));
  Multiplexer #(.select(2), .width(4), .enable("false")) multiplexer_2 (
    .in0(sumador_flags_1_s), .in1(restador_flags_1_s), .in2(andbitabit_1_out_5), .in3(orbitabit_1_out_5),
    .out(S), .sel(OP));
  Hex_Digit_Display hex_digit_display_1 (.value(S));  // open: dp
endmodule

module verificador (
  output [3:0] a,
  output [3:0] b,
  output [1:0] Op,
  output N,
  output Z,
  output V,
  output C,
  output [3:0] Res,
  output halt
);

  wire clock_1_out;

  Clock clock_1 (.out(clock_1_out));
  Counter #(.width(10), .max('h3ff)) counter_1 (
    .Q({Op, b, a}), .carry(halt), .clk(clock_1_out));  // open: load, D, count, clr
  ALUMultiplexorOnly alumultiplexoronly_1 (.A(a), .B(b), .OP(Op), .N(N), .Z(Z), .V(V), .C(C), .S(Res));
endmodule

module and4entradas (
  input  [3:0] A,
  input  in_2,
  output [3:0] out_3
);

  and and_1 (out_3[0], A[0], in_2);
  and and_2 (out_3[1], A[1], in_2);
  and and_3 (out_3[2], A[2], in_2);
  and and_4 (out_3[3], A[3], in_2);
endmodule

module decoder (
  input  [1:0] OP,
  output out_2,
  output out_3,
  output out_4,
  output out_5
);

  wire not_1_out, not_2_out;

  not not_1 (not_1_out, OP[0]);
  not not_2 (not_2_out, OP[1]);
  and and_1 (out_2, not_1_out, not_2_out);
  and and_2 (out_4, not_1_out, OP[1]);
  and and_3 (out_3, OP[0], not_2_out);
  and and_4 (out_5, OP[0], OP[1]);
endmodule

module andbitabit (
  input  [3:0] in_1,
  input  [3:0] in_2,
  output Zero,
  output Z,
  output [3:0] out_5
);

  and and_1 (out_5[0], in_1[0], in_2[0]);
  and and_2 (out_5[1], in_1[1], in_2[1]);
  and and_3 (out_5[2], in_1[2], in_2[2]);
  and and_4 (out_5[3], in_1[3], in_2[3]);
  comparador_cero comparador_cero_1 (.A(out_5), .Z(Z));

  assign Zero = out_5[3];
endmodule

module orbitabit (
  input  [3:0] in_1,
  input  [3:0] in_2,
  output out_3,
  output out_4,
  output [3:0] out_5
);

  or or_1 (out_5[0], in_1[0], in_2[0]);
  or or_2 (out_5[1], in_1[1], in_2[1]);
  or or_3 (out_5[2], in_1[2], in_2[2]);
  or or_4 (out_3, in_1[3], in_2[3]);
  comparador_cero comparador_cero_1 (.A({out_3, out_5[2:0]}), .Z(out_4));

  assign out_5[3] = out_3;
endmodule

module restador_flags (
  input  Cin,
  input  [3:0] A,
  input  [3:0] B,
  output [3:0] S,
  output N,
  output Z,
  output V,
  output C
);

  wire comparador_cero_1_z, not_1_out, not_2_out, sumador_flags_1_c;
  wire [3:0] inversor_4_1_s;

  inversor_4 inversor_4_1 (.A(B), .INV(1'b1), .S(inversor_4_1_s));
  sumador_flags sumador_flags_1 (
    .A(A), .B(inversor_4_1_s), .Cin(Cin), .S(S), .N(N), .Z(Z), .V(V), .C(sumador_flags_1_c));
  comparador_cero comparador_cero_1 (.A(inversor_4_1_s), .Z(comparador_cero_1_z));
  not not_1 (not_1_out, sumador_flags_1_c);
  not not_2 (not_2_out, comparador_cero_1_z);
  and and_1 (C, not_1_out, not_2_out);
  Hex_Digit_Display hex_digit_display_1 (.value(S));  // open: dp
endmodule

module ALUMultiplexorOnly (
  input  [3:0] A,
  input  [3:0] B,
  input  [1:0] OP,
  output N,
  output Z,
  output V,
  output C,
  output [3:0] S
);

  wire [1:0] andbitabit_1_zero, orbitabit_1_out_3;
  wire [3:0] andbitabit_1_out_5, orbitabit_1_out_5, restador_flags_1_n, restador_flags_1_s,
       sumador_flags_1_n, sumador_flags_1_s;

  sumador_flags sumador_flags_1 (
    .A(A), .B(B), .Cin(1'b0), .S(sumador_flags_1_s), .N(sumador_flags_1_n[0]), .Z(sumador_flags_1_n[1]),
    .V(sumador_flags_1_n[2]), .C(sumador_flags_1_n[3]));
  restador_flags restador_flags_1 (
    .A(A), .B(B), .Cin(1'b0), .S(restador_flags_1_s), .N(restador_flags_1_n[0]), .Z(restador_flags_1_n[1]),
    .V(restador_flags_1_n[2]), .C(restador_flags_1_n[3]));
  andbitabit andbitabit_1 (
    .in_1(A), .in_2(B), .out_5(andbitabit_1_out_5), .Zero(andbitabit_1_zero[0]), .Z(andbitabit_1_zero[1]));
  orbitabit orbitabit_1 (
    .in_1(A), .in_2(B), .out_5(orbitabit_1_out_5), .out_3(orbitabit_1_out_3[0]), .out_4(orbitabit_1_out_3[1]));
  Multiplexer #(.select(2), .width(4), .enable("false")) multiplexer_1 (
    .in0(sumador_flags_1_n), .in1(restador_flags_1_n), .in2({2'b00, andbitabit_1_zero}),
    .in3({2'b00, orbitabit_1_out_3}), .out({C, V, Z, N}), .sel(OP));
  Multiplexer #(.select(2), .width(4), .enable("false")) multiplexer_2 (
    .in0(sumador_flags_1_s), .in1(restador_flags_1_s), .in2(andbitabit_1_out_5), .in3(orbitabit_1_out_5),
    .out(S), .sel(OP));
  Hex_Digit_Display hex_digit_display_1 (.value(S));  // open: dp
endmodule
